// Logisim project Contador.circ as structural Verilog: 1 circuit, main circuit main
module main (
);

  wire clock_1_out;
  wire [7:0] random_1_out;

  Clock clock_1 (.out(clock_1_out));
  Random random_1 (.clk(clock_1_out), .out(random_1_out));  // open: next, clr
  Register register_1 (.D(random_1_out), .clk(clock_1_out));  // open: en, Q, clr
endmodule
