// Logisim project Aula3_contador_assincrono_FF-D.circ as structural Verilog: 1 circuit, main circuit main
module main (
);

  wire clock_1_out, Decodificador_p9, Decodificador_p10, Decodificador_p11, Decodificador_p12,
       Decodificador_p13, Decodificador_p14, Decodificador_p15, FF_D_p1, FF_D_p2, FF_D_p4, FF_D_p9, FF_D_p11;

  Clock clock_1 (.out(clock_1_out));
  // _7474 FF_D: pin names not known; wires that end beside it: FF_D_p1, FF_D_p2, clock_1_out, FF_D_p4, FF_D_p2, 1'b0, 1'b1, FF_D_p1, FF_D_p9, FF_D_p2, FF_D_p11, FF_D_p9
  // _7408 AND: pin names not known; wires that end beside it: FF_D_p11, FF_D_p4, FF_D_p1, 1'b0, 1'b1
  // _7448 Decodificador: pin names not known; wires that end beside it: FF_D_p11, 1'b0, 1'b1, 1'b1, 1'b0, FF_D_p4, 1'b0, 1'b1, Decodificador_p9, Decodificador_p10, Decodificador_p11, Decodificador_p12, Decodificador_p13, Decodificador_p14, Decodificador_p15
  _7_Segment_Display u_7_segment_display_1 (
    .g(Decodificador_p10), .f(Decodificador_p9), .a(Decodificador_p11), .b(Decodificador_p12),
    .e(Decodificador_p15), .d(Decodificador_p14), .c(Decodificador_p13));  // open: dp
endmodule
