// Logisim project aula2.circ as structural Verilog: 2 circuits, main circuit main
module main (
  input  in_1,
  input  in_2,
  input  in_3,
  input  in_4,
  input  in_5,
  input  in_6,
  input  in_7,
  input  in_8,
  input  in_9,
  input  in_10,
  input  in_11,
  input  in_12,
  input  in_13,
  input  in_14,
  input  in_15,
  input  in_16,
  input  in_17,
  input  in_18,
  input  A,
  input  B,
  input  Cin
);

  wire n74151_1_p5, n74151_2_p5;

  LED led_1 (.in(n74151_1_p5));
  // _74151 74151_1: pin names not known; wires that end beside it: in_1, in_3, in_7, in_11, n74151_1_p5, in_17, 1'b0, 1'b1, in_5, in_9, in_13, in_15, Cin, B, A
  LED led_2 (.in(n74151_2_p5));
  // _74151 74151_2: pin names not known; wires that end beside it: in_2, in_4, in_8, in_12, n74151_2_p5, in_18, 1'b0, 1'b1, in_6, in_10, in_14, in_16, Cin, B, A
endmodule

module decodificador (
  input  D,
  input  C,
  input  B,
  input  A,
  output a_2,
  output b_2,
  output c_2,
  output d_2,
  output e,
  output f,
  output g
);

  wire and_1_out, and_2_out, and_3_out, and_4_out, and_5_out, and_6_out, and_7_out, and_8_out, and_9_out,
       and_10_out, and_11_out, and_12_out, and_13_out, and_14_out, and_15_out, and_16_out, not_1_out,
       not_2_out, not_3_out, not_4_out, not_5_out, not_6_out, not_7_out, not_8_out, not_9_out, not_10_out,
       not_11_out, not_12_out, not_13_out, not_14_out, not_15_out, not_16_out, not_17_out, not_18_out,
       not_19_out, not_20_out, not_21_out;

  not not_1 (not_1_out, C);
  not not_2 (not_2_out, A);
  not not_3 (not_3_out, B);
  not not_4 (not_4_out, A);
  not not_5 (not_5_out, B);
  not not_6 (not_6_out, C);
  not not_7 (not_7_out, A);
  not not_8 (not_8_out, C);
  not not_9 (not_9_out, A);
  not not_10 (not_10_out, B);
  not not_11 (not_11_out, C);
  not not_12 (not_12_out, A);
  not not_13 (not_13_out, A);
  not not_14 (not_14_out, B);
  not not_15 (not_15_out, A);
  not not_16 (not_16_out, B);
  not not_17 (not_17_out, A);
  not not_18 (not_18_out, C);
  not not_19 (not_19_out, B);
  not not_20 (not_20_out, A);
  and and_1 (and_1_out, not_1_out, not_2_out);
  and and_2 (and_2_out, C, A);
  not not_21 (not_21_out, C);
  and and_3 (and_3_out, not_3_out, not_4_out);
  and and_4 (and_4_out, B, A);
  or or_1 (c_2, not_5_out, A, C);
  and and_5 (and_5_out, not_6_out, not_7_out);
  and and_6 (and_6_out, not_8_out, B);
  and and_7 (and_7_out, B, not_9_out);
  and and_8 (and_8_out, C, not_10_out, A);
  and and_9 (and_9_out, not_11_out, not_12_out);
  and and_10 (and_10_out, B, not_13_out);
  and and_11 (and_11_out, not_14_out, not_15_out);
  and and_12 (and_12_out, C, not_16_out);
  and and_13 (and_13_out, C, not_17_out);
  and and_14 (and_14_out, not_18_out, B);
  and and_15 (and_15_out, C, not_19_out);
  and and_16 (and_16_out, C, not_20_out);
  or or_2 (a_2, and_1_out, B, and_2_out, D);
  or or_3 (b_2, not_21_out, and_3_out, and_4_out);
  or or_4 (d_2, and_5_out, and_6_out, and_7_out, and_8_out);
  or or_5 (e, and_9_out, and_10_out);
  or or_6 (f, and_11_out, and_12_out, and_13_out, D);
  or or_7 (g, and_14_out, and_15_out, and_16_out, D);
  _7_Segment_Display u_7_segment_display_1 (.g(g), .f(f), .a(a_2), .b(b_2), .e(e), .d(d_2), .c(c_2));  // open: dp
endmodule
