// Logisim project Trabalho de SD 2.circ as structural Verilog: 1 circuit, main circuit main
module main (
  input  A1,
  input  A2,
  input  LT___1,
  input  nRBI___0,
  input  A3,
  input  A0,
  input  D,
  output X,
  output Q2,
  output Q0,
  output Q1
);

  wire AND_2_p4, Clock_out, Decodificador_2_p9, Decodificador_2_p10, Decodificador_2_p11,
       Decodificador_2_p12, Decodificador_2_p13, Decodificador_2_p14, Decodificador_2_p15,
       Flip_flops_JK__Q0_e_Q1_p2, Flip_flops_JK__Q0_e_Q1_p15;

  // _7476 Flip_flops_JK: pin names not known
  Clock Clock (.out(Clock_out));
  // _7448 Decodificador: pin names not known
  // _7432 OR: pin names not known
  // _7408 AND: pin names not known
  // _7476 Flip_flops_JK__Q2_e_X: pin names not known; wires that end beside it: 1'b1, Clock_out, Q2, Q2, X
  // _7476 Flip_flops_JK__Q0_e_Q1: pin names not known; wires that end beside it: 1'b1, Flip_flops_JK__Q0_e_Q1_p2, Clock_out, 1'b1, Flip_flops_JK__Q0_e_Q1_p2, 1'b1, 1'b1, Clock_out, 1'b1, Flip_flops_JK__Q0_e_Q1_p2, Q2, 1'b1, Q0, 1'b0, Flip_flops_JK__Q0_e_Q1_p15, Q1, Q1
  // _7486 XOR: pin names not known
  // _7404 NOT: pin names not known
  // _7432 OR_2: pin names not known; wires that end beside it: 1'b0, Flip_flops_JK__Q0_e_Q1_p15, D, Q2, 1'b1
  // _7408 AND_2: pin names not known; wires that end beside it: 1'b0, Flip_flops_JK__Q0_e_Q1_p2, Q1, AND_2_p4, 1'b1
  // _7448 Decodificador_2: pin names not known; wires that end beside it: A1, A2, LT___1, nRBI___0, A3, A0, 1'b0, 1'b1, Decodificador_2_p9, Decodificador_2_p10, Decodificador_2_p11, Decodificador_2_p12, Decodificador_2_p13, Decodificador_2_p14, Decodificador_2_p15
  // _7408 AND_3: pin names not known; wires that end beside it: 1'b0, AND_2_p4, Q2, Q0, 1'b1
  _7_Segment_Display u_7_segment_display_1 (
    .g(Decodificador_2_p10), .f(Decodificador_2_p9), .a(Decodificador_2_p11), .b(Decodificador_2_p12),
    .e(Decodificador_2_p15), .d(Decodificador_2_p14), .c(Decodificador_2_p13));  // open: dp
endmodule
