// Logisim project contador.circ as structural Verilog: 1 circuit, main circuit main
module main (
  input  D
);

  wire Clock_out;

  Clock Clock (.out(Clock_out));
  // _7404 NOT: pin names not known
  // _7408 AND: pin names not known; wires that end beside it: Clock_out
  // _7476 Flip_Flop_JK__Q2: pin names not known; wires that end beside it: D
  // _7432 OR: pin names not known
  // _7476 Flip_Flop_JK__Q1: pin names not known
  // _7476 Flip_Flop_JK__Q0: pin names not known
endmodule
