// Logisim project Trabalho de SD 2.circ as structural Verilog: 4 circuits, main circuit main
module main (
  input  D
);

  wire Clock_out, Decodificador_p9, Decodificador_p10, Decodificador_p11, Decodificador_p12,
       Decodificador_p13, Decodificador_p14, Decodificador_p15, Flip_Flop_JK_Dulpo__X_e_Q2_p4,
       Flip_Flop_JK_Dulpo__X_e_Q2_p5, Flip_Flop_JK_Duplo__Q1_e_Q0_p2, Flip_Flop_JK_Duplo__Q1_e_Q0_p5,
       Flip_Flop_JK_Duplo__Q1_e_Q0_p6, Flip_Flop_JK_Duplo__Q1_e_Q0_p7, Flip_Flop_JK_Duplo__Q1_e_Q0_p9,
       Flip_Flop_JK_Duplo__Q1_e_Q0_p10, Flip_Flop_JK_Duplo__Q1_e_Q0_p11;

  Clock Clock (.out(Clock_out));
  // _7476 Flip_Flop_JK_Dulpo__X_e_Q2: pin names not known; wires that end beside it: 1'b1, Clock_out, 1'b0, Flip_Flop_JK_Dulpo__X_e_Q2_p4, Flip_Flop_JK_Dulpo__X_e_Q2_p5
  // _7476 Flip_Flop_JK_Duplo__Q1_e_Q0: pin names not known; wires that end beside it: Clock_out, Flip_Flop_JK_Duplo__Q1_e_Q0_p2, 1'b1, Clock_out, Flip_Flop_JK_Duplo__Q1_e_Q0_p5, Flip_Flop_JK_Duplo__Q1_e_Q0_p6, Flip_Flop_JK_Duplo__Q1_e_Q0_p7, 1'b0, Flip_Flop_JK_Duplo__Q1_e_Q0_p9, Flip_Flop_JK_Duplo__Q1_e_Q0_p10, Flip_Flop_JK_Duplo__Q1_e_Q0_p11
  J0_e_K0 J0_e_K0 (
    .D(D), .Q2(Flip_Flop_JK_Dulpo__X_e_Q2_p5), .Q1(Flip_Flop_JK_Duplo__Q1_e_Q0_p7), .VCC(1'b1), .GND(1'b0),
    .J0(Flip_Flop_JK_Duplo__Q1_e_Q0_p11), .K0(Flip_Flop_JK_Duplo__Q1_e_Q0_p9));
  J1_e_K1 J1_e_K1 (
    .D(D), .Q2(Flip_Flop_JK_Dulpo__X_e_Q2_p5), .Q0(Flip_Flop_JK_Duplo__Q1_e_Q0_p10), .VCC(1'b1), .GND(1'b0),
    .J1(Flip_Flop_JK_Duplo__Q1_e_Q0_p2), .K1(Flip_Flop_JK_Duplo__Q1_e_Q0_p6));
  J2_e_K2 J2_e_K2 (
    .D(D), .Q1(Flip_Flop_JK_Duplo__Q1_e_Q0_p7), .Q0(Flip_Flop_JK_Duplo__Q1_e_Q0_p10), .VCC(1'b1), .GND(1'b0),
    .J2(Flip_Flop_JK_Duplo__Q1_e_Q0_p5), .K2(Flip_Flop_JK_Dulpo__X_e_Q2_p4));
  // _7448 Decodificador: pin names not known; wires that end beside it: Flip_Flop_JK_Duplo__Q1_e_Q0_p7, Flip_Flop_JK_Dulpo__X_e_Q2_p5, 1'b1, 1'b1, 1'b0, Flip_Flop_JK_Duplo__Q1_e_Q0_p10, 1'b0, 1'b1, Decodificador_p9, Decodificador_p10, Decodificador_p11, Decodificador_p12, Decodificador_p13, Decodificador_p14, Decodificador_p15
  _7_Segment_Display u_7_segment_display_1 (
    .g(Decodificador_p10), .f(Decodificador_p9), .a(Decodificador_p11), .b(Decodificador_p12),
    .e(Decodificador_p15), .d(Decodificador_p14), .c(Decodificador_p13));  // open: dp
endmodule

module J0_e_K0 (
  input  D,
  input  Q2,
  input  Q1,
  input  VCC,
  input  GND,
  output J0,
  output K0
);

  wire AND_2_p2, AND_3_p2, NOT_2_p2, NOT_2_p6, NOT_p2, OR_p2, OR_p7;

  // _7408 AND: pin names not known; wires that end beside it: VCC, D
  // _7404 NOT: pin names not known; wires that end beside it: Q2, NOT_p2, GND, VCC
  // _7408 AND_2: pin names not known; wires that end beside it: Q2, AND_2_p2, GND, VCC, AND_2_p2
  // _7404 NOT_2: pin names not known; wires that end beside it: Q1, NOT_2_p2, GND, VCC, D, NOT_2_p6
  // _7408 AND_3: pin names not known; wires that end beside it: Q1, AND_3_p2, GND, VCC, AND_3_p2
  // _7432 OR: pin names not known; wires that end beside it: NOT_2_p6, OR_p2, GND, VCC, OR_p2, NOT_2_p2, OR_p7, OR_p7, NOT_p2, J0, GND

  assign K0 = VCC;
endmodule

module J1_e_K1 (
  input  D,
  input  Q2,
  input  Q0,
  input  VCC,
  input  GND,
  output J1,
  output K1
);

  wire AND_2_p2, AND_2_p7, AND_p2, AND_p7, NOT_2_p6, NOT_p3, OR_2_p2, OR_2_p7, OR_p2;

  // _7404 NOT: pin names not known; wires that end beside it: VCC, Q0, NOT_p3
  // _7408 AND: pin names not known; wires that end beside it: D, AND_p2, GND, VCC, AND_p2, Q0, AND_p7, NOT_p3
  // _7432 OR: pin names not known; wires that end beside it: D, OR_p2, GND, VCC, OR_p2
  // _7404 NOT_2: pin names not known; wires that end beside it: AND_p7, J1, GND, VCC, Q0, NOT_2_p6
  // _7408 AND_2: pin names not known; wires that end beside it: D, AND_2_p2, GND, VCC, AND_2_p2, Q0, AND_2_p7, D
  // _7432 OR_2: pin names not known; wires that end beside it: NOT_2_p6, OR_2_p2, GND, VCC, OR_2_p2, AND_2_p7, OR_2_p7, OR_2_p7, Q2, K1, GND
endmodule

module J2_e_K2 (
  input  D,
  input  Q1,
  input  Q0,
  input  VCC,
  input  GND,
  output J2,
  output K2
);

  wire AND_2_p2, AND_3_p2, AND_3_p7, AND_4_p2, AND_4_p7, AND_p2, AND_p7, NOT_3_p2, NOT_3_p6, NOT_4_p2,
       NOT_4_p6, OR_2_p2, OR_p2;

  // _7404 NOT: pin names not known; wires that end beside it: VCC
  // _7404 NOT_2: pin names not known; wires that end beside it: VCC
  // _7408 AND: pin names not known; wires that end beside it: D, AND_p2, GND, VCC, AND_p2, Q1, AND_p7, AND_p7
  // _7408 AND_2: pin names not known; wires that end beside it: D, AND_2_p2, GND, VCC, AND_2_p2
  // _7404 NOT_3: pin names not known; wires that end beside it: Q0, NOT_3_p2, GND, VCC, Q1, NOT_3_p6
  // _7404 NOT_4: pin names not known; wires that end beside it: Q1, NOT_4_p2, GND, VCC, Q1, NOT_4_p6
  // _7408 AND_3: pin names not known; wires that end beside it: Q0, AND_3_p2, GND, VCC, AND_3_p2, NOT_3_p6, AND_3_p7, AND_3_p7
  // _7408 AND_4: pin names not known; wires that end beside it: Q0, AND_4_p2, GND, VCC, AND_4_p2, NOT_4_p6, AND_4_p7, AND_4_p7
  // _7432 OR: pin names not known; wires that end beside it: D, OR_p2, GND, VCC, OR_p2, NOT_3_p2, J2, GND
  // _7432 OR_2: pin names not known; wires that end beside it: D, OR_2_p2, GND, VCC, OR_2_p2, NOT_4_p2, K2, GND
endmodule
