// Logisim project Trabalho de SD 3.circ as structural Verilog: 1 circuit, main circuit main
module main (
  input  D
);

  wire AND_2_p2, AND_2_p6, AND_3_p2, AND_3_p6, AND_3_p8, AND_p2, AND_p5, Clock_out, Decodificador_p9,
       Decodificador_p10, Decodificador_p11, Decodificador_p12, Decodificador_p13, Decodificador_p14,
       Decodificador_p15, Flip_Flop_JK_Dulpo__X_e_Q2_p4, Flip_Flop_JK_Dulpo__X_e_Q2_p5,
       Flip_Flop_JK_Duplo__Q1_e_Q0_p4, Flip_Flop_JK_Duplo__Q1_e_Q0_p10, Flip_Flop_JK_Duplo__Q1_e_Q0_p11,
       Flip_Flop_JK_Duplo__Q1_e_Q0_p14, Flip_Flop_JK_Duplo__Q1_e_Q0_p15, OR_p3, OR_p4, OR_p5;

  Clock Clock (.out(Clock_out));
  // _7432 OR: pin names not known; wires that end beside it: 1'b0, 1'b1, OR_p3, OR_p4, OR_p5
  // _7476 Flip_Flop_JK_Dulpo__X_e_Q2: pin names not known; wires that end beside it: 1'b1, Clock_out, 1'b0, Flip_Flop_JK_Dulpo__X_e_Q2_p4, Flip_Flop_JK_Dulpo__X_e_Q2_p5
  // _7476 Flip_Flop_JK_Duplo__Q1_e_Q0: pin names not known; wires that end beside it: OR_p4, Clock_out, OR_p4, Flip_Flop_JK_Duplo__Q1_e_Q0_p4, 1'b1, Clock_out, OR_p5, Flip_Flop_JK_Dulpo__X_e_Q2_p4, Flip_Flop_JK_Duplo__Q1_e_Q0_p4, Flip_Flop_JK_Duplo__Q1_e_Q0_p10, Flip_Flop_JK_Duplo__Q1_e_Q0_p11, 1'b0, 1'b1, Flip_Flop_JK_Duplo__Q1_e_Q0_p14, Flip_Flop_JK_Duplo__Q1_e_Q0_p15, 1'b1
  // _74151 MUX_8x1: pin names not known; wires that end beside it: 1'b0, 1'b0, 1'b0, 1'b0, D, Flip_Flop_JK_Duplo__Q1_e_Q0_p4, Flip_Flop_JK_Duplo__Q1_e_Q0_p14, Flip_Flop_JK_Duplo__Q1_e_Q0_p15, 1'b1
  // _7408 AND: pin names not known; wires that end beside it: 1'b0, AND_p2, Flip_Flop_JK_Duplo__Q1_e_Q0_p10, Flip_Flop_JK_Duplo__Q1_e_Q0_p14, AND_p5, Flip_Flop_JK_Duplo__Q1_e_Q0_p15, Flip_Flop_JK_Duplo__Q1_e_Q0_p11, 1'b1, 1'b0, 1'b0
  // _74151 MUX_8x1_2: pin names not known; wires that end beside it: 1'b0, 1'b0, D, Flip_Flop_JK_Dulpo__X_e_Q2_p4, AND_p2, AND_p5, 1'b1
  // _7408 AND_2: pin names not known; wires that end beside it: 1'b0, AND_2_p2, Flip_Flop_JK_Dulpo__X_e_Q2_p5, Flip_Flop_JK_Duplo__Q1_e_Q0_p10, OR_p3, AND_2_p6, AND_2_p2, D, AND_2_p6, Flip_Flop_JK_Duplo__Q1_e_Q0_p14, 1'b1
  // _7408 AND_3: pin names not known; wires that end beside it: 1'b0, AND_3_p2, Flip_Flop_JK_Dulpo__X_e_Q2_p5, Flip_Flop_JK_Duplo__Q1_e_Q0_p10, OR_p4, AND_3_p6, AND_3_p2, AND_3_p8, AND_3_p6, Flip_Flop_JK_Duplo__Q1_e_Q0_p14, 1'b1
  // _7404 NOT: pin names not known; wires that end beside it: D, AND_3_p8, 1'b0, 1'b1
  // _7448 Decodificador: pin names not known; wires that end beside it: Flip_Flop_JK_Duplo__Q1_e_Q0_p10, Flip_Flop_JK_Dulpo__X_e_Q2_p5, 1'b1, 1'b1, 1'b0, Flip_Flop_JK_Duplo__Q1_e_Q0_p14, 1'b0, 1'b1, Decodificador_p9, Decodificador_p10, Decodificador_p11, Decodificador_p12, Decodificador_p13, Decodificador_p14, Decodificador_p15
  _7_Segment_Display u_7_segment_display_1 (
    .g(Decodificador_p10), .f(Decodificador_p9), .a(Decodificador_p11), .b(Decodificador_p12),
    .e(Decodificador_p15), .d(Decodificador_p14), .c(Decodificador_p13));  // open: dp
endmodule
